// Logisim project Assignment#1(1).circ as structural Verilog: 3 circuits, main circuit counter
module counter (
  input  in_1,
  input  in_2,
  output out_3,
  output out_4,
  output out_5,
  output out_6,
  output S1,
  output S2,
  output S3,
  output S4
);

  wire and_1_out, and_2_out, and_3_out, and_4_out, and_5_out, C1_2_out, C1_3_out, C1_out, C2_2_out, C2_out,
       C3_out, C12_out, C13_out, C23_out, d_ff_5_qn, d_ff_6_qn, d_ff_7_qn, d_ff_8_qn, not_1_out, not_2_out,
       not_3_out, not_4_out, not_5_out, not_6_out, not_7_out, not_8_out, not_9_out, not_10_out, not_11_out,
       not_12_out, not_13_out, not_14_out, not_15_out, not_16_out, not_17_out, not_18_out, not_19_out,
       not_20_out, not_21_out, not_22_out, not_23_out, not_24_out, not_25_out, not_26_out, not_27_out,
       not_28_out, not_29_out, not_30_out, not_31_out, or_1_out, or_2_out, or_3_out, or_4_out;

  not not_1 (not_1_out, S1);
  not not_2 (not_2_out, S2);
  not not_3 (not_3_out, S3);
  not not_4 (not_4_out, S1);
  not not_5 (not_5_out, S2);
  not not_6 (not_6_out, S4);
  not not_7 (not_7_out, S1);
  not not_8 (not_8_out, S4);
  not not_9 (not_9_out, S2);
  not not_10 (not_10_out, S4);
  not not_11 (not_11_out, S2);
  not not_12 (not_12_out, S2);
  not not_13 (not_13_out, S3);
  and and_1 (and_1_out, not_1_out, not_2_out, not_3_out, S4);
  and C3 (C3_out, not_4_out, not_5_out, S3, not_6_out);
  and C23 (C23_out, not_7_out, S2, S3, not_8_out);
  and C13 (C13_out, S1, not_9_out, S3, not_10_out);
  and C1 (C1_out, S1, not_11_out, S3, S4);
  and C1_2 (C1_2_out, S1, not_12_out, not_13_out, S4);
  not not_14 (not_14_out, S1);
  not not_15 (not_15_out, S1);
  not not_16 (not_16_out, S2);
  not not_17 (not_17_out, S1);
  not not_18 (not_18_out, S3);
  not not_19 (not_19_out, S1);
  not not_20 (not_20_out, S2);
  not not_21 (not_21_out, S3);
  not not_22 (not_22_out, S4);
  not not_23 (not_23_out, S1);
  not not_24 (not_24_out, S3);
  not not_25 (not_25_out, S4);
  not not_26 (not_26_out, S2);
  not not_27 (not_27_out, S3);
  not not_28 (not_28_out, S4);
  not not_29 (not_29_out, S3);
  not not_30 (not_30_out, S4);
  and and_2 (and_2_out, not_14_out, S2, S3, S4);
  and and_3 (and_3_out, not_15_out, not_16_out, S3, S4);
  and C2 (C2_out, not_17_out, S2, not_18_out, S4);
  and and_4 (and_4_out, not_19_out, not_20_out, not_21_out, not_22_out);
  and C2_2 (C2_2_out, not_23_out, S2, not_24_out, not_25_out);
  and C1_3 (C1_3_out, S1, not_26_out, not_27_out, not_28_out);
  and C12 (C12_out, S1, S2, not_29_out, not_30_out);
  or or_1 (or_1_out, and_2_out, C1_out, C1_2_out, C1_3_out, C13_out, C12_out);
  or or_2 (or_2_out, C1_out, and_3_out, C2_out, C12_out, C2_2_out, C23_out);
  or or_3 (or_3_out, C1_2_out, C2_out, and_1_out, C3_out, C23_out, C13_out);
  or or_4 (or_4_out, and_4_out, C2_2_out, C3_out, C23_out, C1_3_out, C13_out, C12_out);
  D_Flip_Flop d_ff_1 (.clk(in_1), .D(or_1_out), .Q(S1));  // open: Qn, preset, en, reset
  D_Flip_Flop d_ff_2 (.clk(in_1), .D(or_2_out), .Q(S2));  // open: Qn, preset, en, reset
  D_Flip_Flop d_ff_3 (.clk(in_1), .D(or_3_out), .Q(S3));  // open: Qn, preset, en, reset
  D_Flip_Flop d_ff_4 (.clk(in_1), .D(or_4_out), .Q(S4));  // open: Qn, preset, en, reset
  not not_31 (not_31_out, out_3);
  and and_5 (and_5_out, not_31_out, out_5, out_6, out_4);
  D_Flip_Flop d_ff_5 (.clk(in_2), .D(d_ff_5_qn), .Q(out_3), .Qn(d_ff_5_qn), .reset(and_5_out));  // open: preset, en
  D_Flip_Flop d_ff_6 (
    .clk(d_ff_5_qn), .D(d_ff_6_qn), .Q(out_4), .Qn(d_ff_6_qn), .reset(and_5_out));  // open: preset, en
  D_Flip_Flop d_ff_7 (
    .clk(d_ff_6_qn), .D(d_ff_7_qn), .Q(out_5), .Qn(d_ff_7_qn), .reset(and_5_out));  // open: preset, en
  D_Flip_Flop d_ff_8 (
    .clk(d_ff_7_qn), .D(d_ff_8_qn), .Q(out_6), .Qn(d_ff_8_qn), .reset(and_5_out));  // open: preset, en
endmodule

module controller (
  input  X,
  input  Y,
  input  Z,
  input  W,
  output State2,
  output State3,
  output State1,
  output State4,
  output Sate5
);

  wire not_1_out, not_2_out, not_3_out, not_4_out, S1_out, S2_out, S3_out, S4_out, S5_out, S6_out, S7_out,
       S8_out, S9_out, S10_out, S11_out, S13_out;

  not not_1 (not_1_out, X);
  not not_2 (not_2_out, Y);
  not not_3 (not_3_out, Z);
  not not_4 (not_4_out, W);
  // AND_Gate S0 has open pins: in0=not_1_out, in1=not_2_out, in2=not_3_out, in3=not_4_out, out=open
  and S1 (S1_out, not_1_out, not_2_out, not_3_out, W);
  and S2 (S2_out, not_1_out, not_2_out, Z, not_4_out);
  and S3 (S3_out, not_1_out, not_2_out, Z, W);
  and S4 (S4_out, not_1_out, Y, not_3_out, not_4_out);
  and S5 (S5_out, not_1_out, Y, not_3_out, W);
  and S6 (S6_out, not_1_out, Y, Z, not_4_out);
  and S7 (S7_out, not_1_out, Y, Z, W);
  and S8 (S8_out, X, not_2_out, not_3_out, not_4_out);
  and S9 (S9_out, X, not_2_out, not_3_out, W);
  and S10 (S10_out, X, not_2_out, Z, not_4_out);
  and S11 (S11_out, X, not_2_out, Z, W);
  // AND_Gate S12 has open pins: in0=X, in1=Y, in2=not_3_out, in3=not_4_out, out=open
  and S13 (S13_out, X, Y, not_3_out, W);
  // AND_Gate S14 has open pins: in0=X, in1=Y, in2=Z, in3=not_4_out, out=open
  // AND_Gate S15 has open pins: in0=X, in1=Y, in2=Z, in3=W, out=open
  or or_1 (State2, S3_out, S11_out, S13_out, S4_out);
  or or_2 (State3, S5_out, S13_out, S11_out, S6_out);
  or or_3 (State4, S7_out, S8_out, S13_out, S11_out);
  or or_4 (Sate5, S9_out, S10_out, S11_out, S13_out);
  or or_5 (State1, S1_out, S2_out, S3_out, S4_out, S5_out, S6_out, S7_out, S8_out, S9_out, S10_out, S11_out, S13_out);
endmodule

module circuit (
);

  wire controller_1_sate5, controller_1_state1, controller_1_state2, controller_1_state3,
       controller_1_state4, undriven, undriven_2, undriven_3, undriven_4;

  Clock clock_1 ();  // open: out
  controller controller_1 (
    .X(undriven_4), .Y(undriven_3), .Z(undriven_2), .W(undriven), .State2(controller_1_state2),
    .State3(controller_1_state3), .State1(controller_1_state1), .State4(controller_1_state4),
    .Sate5(controller_1_sate5));
  LED led_1 (.in(controller_1_state1));
  LED led_2 (.in(controller_1_state1));
  LED led_3 (.in(controller_1_state1));
  LED led_4 (.in(controller_1_state1));
  LED led_5 (.in(controller_1_state1));
  LED led_6 (.in(controller_1_state1));
  LED led_7 (.in(controller_1_state1));
  LED led_8 (.in(controller_1_state1));
  LED led_9 (.in(controller_1_state1));
  LED led_10 (.in(controller_1_state1));
  LED led_11 (.in(controller_1_state1));
  LED led_12 (.in(controller_1_state1));
  LED led_13 (.in(controller_1_state1));
  LED led_14 (.in(controller_1_state1));
  LED led_15 (.in(controller_1_state1));
  LED led_16 (.in(controller_1_state1));
  LED led_17 (.in(controller_1_state1));
  LED led_18 (.in(controller_1_state2));
  LED led_19 (.in(controller_1_state2));
  LED led_20 (.in(controller_1_state1));
  LED led_21 (.in(controller_1_state1));
  LED led_22 (.in(controller_1_state1));
  LED led_23 (.in(controller_1_state1));
  LED led_24 (.in(controller_1_state2));
  LED led_25 (.in(controller_1_state2));
  LED led_26 (.in(controller_1_state3));
  LED led_27 (.in(controller_1_state3));
  LED led_28 (.in(controller_1_state2));
  LED led_29 (.in(controller_1_state2));
  LED led_30 (.in(controller_1_state2));
  LED led_31 (.in(controller_1_state2));
  LED led_32 (.in(controller_1_state2));
  LED led_33 (.in(controller_1_state3));
  LED led_34 (.in(controller_1_state3));
  LED led_35 (.in(controller_1_state4));
  LED led_36 (.in(controller_1_state3));
  LED led_37 (.in(controller_1_state3));
  LED led_38 (.in(controller_1_state3));
  LED led_39 (.in(controller_1_state3));
  LED led_40 (.in(controller_1_state3));
  LED led_41 (.in(controller_1_state4));
  LED led_42 (.in(controller_1_sate5));
  LED led_43 (.in(controller_1_state4));
  LED led_44 (.in(controller_1_state4));
  LED led_45 (.in(controller_1_state4));
  LED led_46 (.in(controller_1_state4));
  LED led_47 (.in(controller_1_state4));
  LED led_48 (.in(controller_1_state4));
  LED led_49 (.in(controller_1_state4));
  LED led_50 (.in(controller_1_sate5));
  LED led_51 (.in(controller_1_sate5));
  LED led_52 (.in(controller_1_sate5));
  LED led_53 (.in(controller_1_sate5));
  LED led_54 (.in(controller_1_sate5));
  LED led_55 (.in(controller_1_sate5));
  LED led_56 (.in(controller_1_sate5));
  LED led_57 (.in(controller_1_sate5));

  // Notes on the sheet:
  //   Counter
  //   Controller
  //   State 1
  //   State 2
  //   State 3
  //   State 4
  //   State 5
endmodule
