// Logisim project Assignment#1.circ as structural Verilog: 3 circuits, main circuit Counter
module Counter (
  input  l0,
  output S0,
  output S1,
  output S2,
  output S3
);

  wire and_1_out, and_2_out, and_3_out, and_4_out, and_5_out, and_6_out, and_7_out, and_8_out, and_9_out,
       and_10_out, and_11_out, and_12_out, and_13_out, not_1_out, not_2_out, not_3_out, not_4_out, not_5_out,
       not_6_out, not_7_out, not_8_out, not_9_out, not_10_out, not_11_out, not_12_out, not_13_out,
       not_14_out, not_15_out, not_16_out, not_17_out, not_18_out, not_19_out, not_20_out, not_21_out,
       not_22_out, not_23_out, not_24_out, not_25_out, not_26_out, not_27_out, not_28_out, not_29_out,
       not_30_out, or_1_out, or_2_out, or_3_out, or_4_out;

  not not_1 (not_1_out, S1);
  not not_2 (not_2_out, S1);
  not not_3 (not_3_out, S2);
  not not_4 (not_4_out, S0);
  not not_5 (not_5_out, S1);
  not not_6 (not_6_out, S2);
  not not_7 (not_7_out, S0);
  not not_8 (not_8_out, S1);
  not not_9 (not_9_out, S3);
  not not_10 (not_10_out, S0);
  not not_11 (not_11_out, S3);
  not not_12 (not_12_out, S1);
  not not_13 (not_13_out, S3);
  and and_1 (and_1_out, S0, not_1_out, S2, S3);
  and and_2 (and_2_out, S0, not_2_out, not_3_out, S3);
  and and_3 (and_3_out, not_4_out, not_5_out, not_6_out, S3);
  and and_4 (and_4_out, not_7_out, not_8_out, S2, not_9_out);
  and and_5 (and_5_out, not_10_out, S1, S2, not_11_out);
  and and_6 (and_6_out, S0, not_12_out, S2, not_13_out);
  not not_14 (not_14_out, S0);
  not not_15 (not_15_out, S0);
  not not_16 (not_16_out, S1);
  not not_17 (not_17_out, S0);
  not not_18 (not_18_out, S2);
  not not_19 (not_19_out, S0);
  not not_20 (not_20_out, S1);
  not not_21 (not_21_out, S2);
  not not_22 (not_22_out, S3);
  not not_23 (not_23_out, S0);
  not not_24 (not_24_out, S2);
  not not_25 (not_25_out, S3);
  not not_26 (not_26_out, S1);
  not not_27 (not_27_out, S2);
  not not_28 (not_28_out, S3);
  not not_29 (not_29_out, S2);
  not not_30 (not_30_out, S3);
  and and_7 (and_7_out, not_14_out, S1, S2, S3);
  and and_8 (and_8_out, not_15_out, not_16_out, S2, S3);
  and and_9 (and_9_out, not_17_out, S1, not_18_out, S3);
  and and_10 (and_10_out, not_19_out, not_20_out, not_21_out, not_22_out);
  and and_11 (and_11_out, not_23_out, S1, not_24_out, not_25_out);
  and and_12 (and_12_out, S0, not_26_out, not_27_out, not_28_out);
  and and_13 (and_13_out, S0, S1, not_29_out, not_30_out);
  or or_1 (or_1_out, and_7_out, and_1_out, and_2_out, and_12_out, and_6_out, and_13_out);
  or or_2 (or_2_out, and_1_out, and_8_out, and_9_out, and_13_out, and_11_out, and_5_out);
  or or_3 (or_3_out, and_2_out, and_9_out, and_3_out, and_4_out, and_5_out, and_6_out);
  or or_4 (or_4_out, and_10_out, and_11_out, and_4_out, and_5_out, and_12_out, and_6_out, and_13_out);
  D_Flip_Flop d_ff_1 (.clk(l0), .D(or_1_out), .Q(S0));  // open: Qn, preset, en, reset
  D_Flip_Flop d_ff_2 (.clk(l0), .D(or_2_out), .Q(S1));  // open: Qn, preset, en, reset
  D_Flip_Flop d_ff_3 (.clk(l0), .D(or_3_out), .Q(S2));  // open: Qn, preset, en, reset
  D_Flip_Flop d_ff_4 (.clk(l0), .D(or_4_out), .Q(S3));  // open: Qn, preset, en, reset
endmodule

module Controller (
  input  l0,
  input  l1,
  input  l2,
  input  l3,
  output State2,
  output State3,
  output State1,
  output State4,
  output Sate5
);

  wire not_1_out, not_2_out, not_3_out, not_4_out, S1_out, S2_out, S3_out, S4_out, S5_out, S6_out, S7_out,
       S8_out, S9_out, S10_out, S11_out, S13_out;

  not not_1 (not_1_out, l0);
  not not_2 (not_2_out, l1);
  not not_3 (not_3_out, l2);
  not not_4 (not_4_out, l3);
  // AND_Gate S0 has open pins: in0=not_1_out, in1=not_2_out, in2=not_3_out, in3=not_4_out, out=open
  and S1 (S1_out, not_1_out, not_2_out, not_3_out, l3);
  and S2 (S2_out, not_1_out, not_2_out, l2, not_4_out);
  and S3 (S3_out, not_1_out, not_2_out, l2, l3);
  and S4 (S4_out, not_1_out, l1, not_3_out, not_4_out);
  and S5 (S5_out, not_1_out, l1, not_3_out, l3);
  and S6 (S6_out, not_1_out, l1, l2, not_4_out);
  and S7 (S7_out, not_1_out, l1, l2, l3);
  and S8 (S8_out, l0, not_2_out, not_3_out, not_4_out);
  and S9 (S9_out, l0, not_2_out, not_3_out, l3);
  and S10 (S10_out, l0, not_2_out, l2, not_4_out);
  and S11 (S11_out, l0, not_2_out, l2, l3);
  // AND_Gate S12 has open pins: in0=l0, in1=l1, in2=not_3_out, in3=not_4_out, out=open
  and S13 (S13_out, l0, l1, not_3_out, l3);
  // AND_Gate S14 has open pins: in0=l0, in1=l1, in2=l2, in3=not_4_out, out=open
  // AND_Gate S15 has open pins: in0=l0, in1=l1, in2=l2, in3=l3, out=open
  or or_1 (State2, S3_out, S11_out, S13_out, S4_out);
  or or_2 (State3, S5_out, S13_out, S11_out, S6_out);
  or or_3 (State4, S7_out, S8_out, S13_out, S11_out);
  or or_4 (Sate5, S9_out, S10_out, S11_out, S13_out);
  or or_5 (State1, S1_out, S2_out, S3_out, S4_out, S5_out, S6_out, S7_out, S8_out, S9_out, S10_out, S11_out, S13_out);
endmodule

module Circuit (
);

  wire clock_1_out, controller_1_sate5, controller_1_state1, controller_1_state2, controller_1_state3,
       controller_1_state4, counter_1_s0, counter_1_s1, counter_1_s2, counter_1_s3;

  Clock clock_1 (.out(clock_1_out));
  Counter counter_1 (.l0(clock_1_out), .S0(counter_1_s0), .S1(counter_1_s1), .S2(counter_1_s2), .S3(counter_1_s3));
  Controller controller_1 (
    .l0(counter_1_s0), .l1(counter_1_s1), .l2(counter_1_s2), .l3(counter_1_s3), .State2(controller_1_state2),
    .State3(controller_1_state3), .State1(controller_1_state1), .State4(controller_1_state4),
    .Sate5(controller_1_sate5));
  LED led_1 (.in(controller_1_state1));
  LED led_2 (.in(controller_1_state1));
  LED led_3 (.in(controller_1_state1));
  LED led_4 (.in(controller_1_state1));
  LED led_5 (.in(controller_1_state1));
  LED led_6 (.in(controller_1_state1));
  LED led_7 (.in(controller_1_state1));
  LED led_8 (.in(controller_1_state1));
  LED led_9 (.in(controller_1_state1));
  LED led_10 (.in(controller_1_state1));
  LED led_11 (.in(controller_1_state1));
  LED led_12 (.in(controller_1_state1));
  LED led_13 (.in(controller_1_state1));
  LED led_14 (.in(controller_1_state1));
  LED led_15 (.in(controller_1_state1));
  LED led_16 (.in(controller_1_state1));
  LED led_17 (.in(controller_1_state1));
  LED led_18 (.in(controller_1_state2));
  LED led_19 (.in(controller_1_state2));
  LED led_20 (.in(controller_1_state1));
  LED led_21 (.in(controller_1_state1));
  LED led_22 (.in(controller_1_state1));
  LED led_23 (.in(controller_1_state1));
  LED led_24 (.in(controller_1_state2));
  LED led_25 (.in(controller_1_state2));
  LED led_26 (.in(controller_1_state3));
  LED led_27 (.in(controller_1_state2));
  LED led_28 (.in(controller_1_state2));
  LED led_29 (.in(controller_1_state2));
  LED led_30 (.in(controller_1_state2));
  LED led_31 (.in(controller_1_state2));
  LED led_32 (.in(controller_1_state3));
  LED led_33 (.in(controller_1_state3));
  LED led_34 (.in(controller_1_state4));
  LED led_35 (.in(controller_1_state3));
  LED led_36 (.in(controller_1_state3));
  LED led_37 (.in(controller_1_state3));
  LED led_38 (.in(controller_1_state3));
  LED led_39 (.in(controller_1_state3));
  LED led_40 (.in(controller_1_state3));
  LED led_41 (.in(controller_1_state4));
  LED led_42 (.in(controller_1_state4));
  LED led_43 (.in(controller_1_state4));
  LED led_44 (.in(controller_1_state4));
  LED led_45 (.in(controller_1_state4));
  LED led_46 (.in(controller_1_state4));
  LED led_47 (.in(controller_1_state4));
  LED led_48 (.in(controller_1_state4));
  LED led_49 (.in(controller_1_sate5));
  LED led_50 (.in(controller_1_sate5));
  LED led_51 (.in(controller_1_sate5));
  LED led_52 (.in(controller_1_sate5));
  LED led_53 (.in(controller_1_sate5));
  LED led_54 (.in(controller_1_sate5));
  LED led_55 (.in(controller_1_sate5));
  LED led_56 (.in(controller_1_sate5));
  LED led_57 (.in(controller_1_sate5));

  // Notes on the sheet:
  //   Clock
  //   Counter
  //   Controller
  //   State 1
  //   State 2
  //   State 3
  //   State 4
  //   State 5
endmodule
