// Logisim project a.circ as structural Verilog
module decoder (
  input  l0,
  input  l1,
  output S0,
  output S1,
  output S2,
  output S3
);

  wire not_1_out, not_2_out;

  not not_1 (not_1_out, l0);
  not not_2 (not_2_out, l1);
  and and_1 (S0, not_1_out, not_2_out);
  and and_2 (S1, l0, not_2_out);
  and and_3 (S2, not_1_out, l1);
  and and_4 (S3, l0, l1);
endmodule

module multiplexers (
  input  [3:0] in_1,
  input  [3:0] in_2,
  input  [3:0] in_3,
  input  [3:0] in_4,
  input  [3:0] in_5,
  input  [3:0] in_6,
  output [3:0] out_7
);

  wire and_1_out, and_2_out, and_3_out, and_4_out, decoder_1_p3, decoder_1_p4, decoder_1_p5, decoder_1_p6;

  // decoder decoder_1: pin names not known; wires that end beside it: in_3, in_4, decoder_1_p3, decoder_1_p4, decoder_1_p5, decoder_1_p6
  and and_1 (and_1_out, in_1[0], decoder_1_p3);
  and and_2 (and_2_out, in_2[0], decoder_1_p4);
  and and_3 (and_3_out, decoder_1_p5, in_5[0]);
  and and_4 (and_4_out, decoder_1_p6, in_6[0]);
  or or_1 (out_7[0], and_1_out, and_2_out, and_3_out, and_4_out);
  // Pins of 1 and 4 bits meet at in_2
  // Pins of 1 and 4 bits meet at in_6
  // Pins of 1 and 4 bits meet at out_7
  // Pins of 1 and 4 bits meet at in_1
  // Pins of 1 and 4 bits meet at in_5
endmodule
