// Logisim project b.circ as structural Verilog
module main (
  input  D,
  input  E,
  output minus_Q,
  output Q
);

  wire and_1_out, and_2_out, not_1_out;

  not not_1 (not_1_out, D);
  and and_1 (and_1_out, D, E);
  and and_2 (and_2_out, E, not_1_out);
  nor nor_1 (minus_Q, and_1_out, Q);
  nor nor_2 (Q, minus_Q, and_2_out);
endmodule
